// Logisim project processor.circ as structural Verilog: 31 circuits, main circuit main
module main (
  output ZF,
  output CF,
  output OF,
  output [19:0] Current_Instruction
);

  wire and_1_out, and_2_out, and_3_out, and_4_out, clock_1_out, control_unit_1_out_3, control_unit_1_out_5,
       control_unit_1_out_6, control_unit_1_out_7, control_unit_1_out_8, control_unit_1_out_9,
       control_unit_1_out_10, control_unit_1_out_11, control_unit_1_out_12, control_unit_1_out_13,
       control_unit_1_out_14, control_unit_1_out_15, control_unit_1_out_16, control_unit_1_out_17,
       control_unit_1_out_18, control_unit_1_out_19, control_unit_1_out_20, control_unit_1_out_21,
       control_unit_1_out_22, control_unit_1_out_23, control_unit_1_out_24, control_unit_1_out_25,
       control_unit_1_out_26, control_unit_1_out_27, not_1_out, or_1_out, xor_1_out;
  wire [1:0] layout_select_1_out;
  wire [2:0] aluop_1_out;
  wire [3:0] multiplexer_1_out, multiplexer_1_out_2, multiplexer_1_out_3;
  wire [9:0] address_register_1_out, program_counter_1_out_7, ram_1_data;
  wire [19:0] address_extender_1_out, multiplexer_2_out, multiplexer_3_out, multiplexer_4_out,
       register_file_1_out1, register_file_1_out2, rom_1_data, sign_extender_1_out;
  wire [19:10] ram_1_data_2;

  Clock clock_1 (.out(clock_1_out));
  and and_1 (and_1_out, clock_1_out, ~control_unit_1_out_24);  // AND_Gate
  not not_1 (not_1_out, and_1_out);
  Control_Unit control_unit_1 (
    .CLK(not_1_out), .Opcode(Current_Instruction[19:16]), .out_3(control_unit_1_out_3),
    .out_5(control_unit_1_out_5), .out_6(control_unit_1_out_6), .out_7(control_unit_1_out_7),
    .out_8(control_unit_1_out_8), .out_9(control_unit_1_out_9), .out_10(control_unit_1_out_10),
    .out_11(control_unit_1_out_11), .out_12(control_unit_1_out_12), .out_13(control_unit_1_out_13),
    .out_14(control_unit_1_out_14), .out_15(control_unit_1_out_15), .out_16(control_unit_1_out_16),
    .out_17(control_unit_1_out_17), .out_18(control_unit_1_out_18), .out_19(control_unit_1_out_19),
    .out_20(control_unit_1_out_20), .out_21(control_unit_1_out_21), .out_22(control_unit_1_out_22),
    .out_23(control_unit_1_out_23), .out_24(control_unit_1_out_24), .out_25(control_unit_1_out_25),
    .out_26(control_unit_1_out_26), .out_27(control_unit_1_out_27));  // open: out_4
  Program_Counter program_counter_1 (
    .LD(or_1_out), .ADDR(ram_1_data), .INC(control_unit_1_out_3), .out_7(program_counter_1_out_7),
    .CLK(and_1_out), .RST(control_unit_1_out_5), .RD(control_unit_1_out_6));
  Address_Register address_register_1 (
    .CLK(and_1_out), .IN({{8{1'b0}}, Current_Instruction[11:0]}), .ENB(control_unit_1_out_7),
    .RST(control_unit_1_out_8), .RD(control_unit_1_out_9), .OUT(address_register_1_out));
  ROM #(.addrWidth(10), .dataWidth(20)) rom_1 (
    .addr(program_counter_1_out_7), .data(rom_1_data), .sel(control_unit_1_out_10));
  RAM #(.addrWidth(10), .dataWidth(20), .bus("separate")) ram_1 (
    .addr(address_register_1_out), .din({ram_1_data_2, ram_1_data}), .data({ram_1_data_2, ram_1_data}),
    .str(control_unit_1_out_11), .sel(control_unit_1_out_12), .clk(and_1_out), .ld(control_unit_1_out_13),
    .clr(control_unit_1_out_14));
  Address_Extender address_extender_1 (.IN(program_counter_1_out_7), .OUT(address_extender_1_out));
  Register register_1 (
    .CLK(and_1_out), .IN(rom_1_data), .ENB(control_unit_1_out_25), .RST(control_unit_1_out_26),
    .OUT(Current_Instruction));
  RdRegister rdregister_1 (
    .CLK(and_1_out), .IN({ram_1_data_2, ram_1_data}), .WR(control_unit_1_out_15),
    .RST(control_unit_1_out_16), .RD(control_unit_1_out_17), .OUT({ram_1_data_2, ram_1_data}));
  Multiplexer #(.select(2), .width(12), .enable("false")) multiplexer_1 (
    .in0({Current_Instruction[15:12], Current_Instruction[3:0], Current_Instruction[11:8]}),
    .in1({Current_Instruction[11:8], Current_Instruction[3:0], Current_Instruction[15:12]}),
    .in2({Current_Instruction[3:0], Current_Instruction[11:8], Current_Instruction[15:12]}),
    .out({multiplexer_1_out_3, multiplexer_1_out_2, multiplexer_1_out}), .sel(layout_select_1_out));  // open: in3
  Layout_Select layout_select_1 (.IN(Current_Instruction[19:16]), .OUT(layout_select_1_out));
  assign {ram_1_data_2, ram_1_data} = and_2_out ? register_file_1_out1 : 20'bz;  // Controlled_Buffer controlled_buffer_1
  Register_File register_file_1 (
    .CLK(and_1_out), .LENB(control_unit_1_out_18), .LADDR(multiplexer_1_out_3),
    .R2ENB(control_unit_1_out_19), .R2ADDR(multiplexer_1_out_2), .R1ENB(control_unit_1_out_20),
    .R1ADDR(multiplexer_1_out), .IN({ram_1_data_2, ram_1_data}), .RST(control_unit_1_out_21),
    .OUT1(register_file_1_out1), .OUT2(register_file_1_out2));
  Multiplexer #(.width(20), .enable("false")) multiplexer_2 (
    .in0(register_file_1_out2), .in1(sign_extender_1_out), .out(multiplexer_2_out),
    .sel(Current_Instruction[7]));
  Sign_Extender sign_extender_1 (.IN(Current_Instruction[6:0]), .OUT(sign_extender_1_out));
  and and_2 (and_2_out, control_unit_1_out_20, ~control_unit_1_out_23);  // AND_Gate
  or or_1 (or_1_out, control_unit_1_out_22, and_3_out);
  Multiplexer #(.width(20), .enable("false")) multiplexer_3 (
    .in0(register_file_1_out1), .in1(address_extender_1_out), .out(multiplexer_3_out),
    .sel(control_unit_1_out_22));
  ALU alu_1 (
    .IN1(multiplexer_3_out), .RENB(control_unit_1_out_23), .IN2(multiplexer_4_out),
    .OUT({ram_1_data_2, ram_1_data}), .Zero(ZF), .Carry(CF), .Overflow(OF), .OP(aluop_1_out));
  Multiplexer #(.width(20), .enable("false")) multiplexer_4 (
    .in0(multiplexer_2_out), .in1({{5{Current_Instruction[15]}}, Current_Instruction[14:0]}),
    .out(multiplexer_4_out), .sel(control_unit_1_out_22));
  ALUOp aluop_1 (.IN(Current_Instruction[19:16]), .OUT(aluop_1_out));
  assign {ram_1_data_2, ram_1_data} = and_3_out ? {{12{1'b0}}, Current_Instruction[7:0]} : 20'bz;  // Controlled_Buffer controlled_buffer_2
  and and_3 (and_3_out, control_unit_1_out_27, xor_1_out);
  xor xor_1 (xor_1_out, ZF, and_4_out);
  and and_4 (and_4_out, Current_Instruction[18], Current_Instruction[19]);

  // Notes on the sheet:
  //   Instruction Memory
  //   contents of rom_1 (hex, n*v repeats v):
  //   51101 52202 12281 72000 13102 73001 62001 61000 8fffa
  //   Data Memory
  //   IR
  //   MDR
endmodule

module HalfAdder (
  input  IN1,
  input  IN2,
  output SUM,
  output COUT
);

  xor xor_1 (SUM, IN1, IN2);
  and and_1 (COUT, IN1, IN2);
endmodule

module FullAdder (
  input  CIN,
  input  IN1,
  input  IN2,
  output SUM,
  output COUT
);

  wire and_1_out, and_2_out, xor_1_out;

  xor xor_1 (xor_1_out, IN1, IN2);
  xor xor_2 (SUM, xor_1_out, CIN);
  and and_1 (and_1_out, xor_1_out, CIN);
  and and_2 (and_2_out, IN1, IN2);
  or or_1 (COUT, and_1_out, and_2_out);
endmodule

module Register (
  input  CLK,
  input  [19:0] IN,
  input  ENB,
  input  RST,
  output [19:0] OUT
);

  D_Flip_Flop_part d_ff_1 (.clk(CLK), .D(IN[0]), .Q(OUT[0]), .en(ENB), .reset(RST));  // open: Qn, preset
  D_Flip_Flop_part d_ff_2 (.clk(CLK), .D(IN[5]), .Q(OUT[5]), .en(ENB), .reset(RST));  // open: Qn, preset
  D_Flip_Flop_part d_ff_3 (.clk(CLK), .D(IN[10]), .Q(OUT[10]), .en(ENB), .reset(RST));  // open: Qn, preset
  D_Flip_Flop_part d_ff_4 (.clk(CLK), .D(IN[15]), .Q(OUT[15]), .en(ENB), .reset(RST));  // open: Qn, preset
  D_Flip_Flop_part d_ff_5 (.clk(CLK), .D(IN[1]), .Q(OUT[1]), .en(ENB), .reset(RST));  // open: Qn, preset
  D_Flip_Flop_part d_ff_6 (.clk(CLK), .D(IN[6]), .Q(OUT[6]), .en(ENB), .reset(RST));  // open: Qn, preset
  D_Flip_Flop_part d_ff_7 (.clk(CLK), .D(IN[11]), .Q(OUT[11]), .en(ENB), .reset(RST));  // open: Qn, preset
  D_Flip_Flop_part d_ff_8 (.clk(CLK), .D(IN[16]), .Q(OUT[16]), .en(ENB), .reset(RST));  // open: Qn, preset
  D_Flip_Flop_part d_ff_9 (.clk(CLK), .D(IN[2]), .Q(OUT[2]), .en(ENB), .reset(RST));  // open: Qn, preset
  D_Flip_Flop_part d_ff_10 (.clk(CLK), .D(IN[7]), .Q(OUT[7]), .en(ENB), .reset(RST));  // open: Qn, preset
  D_Flip_Flop_part d_ff_11 (.clk(CLK), .D(IN[12]), .Q(OUT[12]), .en(ENB), .reset(RST));  // open: Qn, preset
  D_Flip_Flop_part d_ff_12 (.clk(CLK), .D(IN[17]), .Q(OUT[17]), .en(ENB), .reset(RST));  // open: Qn, preset
  D_Flip_Flop_part d_ff_13 (.clk(CLK), .D(IN[3]), .Q(OUT[3]), .en(ENB), .reset(RST));  // open: Qn, preset
  D_Flip_Flop_part d_ff_14 (.clk(CLK), .D(IN[8]), .Q(OUT[8]), .en(ENB), .reset(RST));  // open: Qn, preset
  D_Flip_Flop_part d_ff_15 (.clk(CLK), .D(IN[13]), .Q(OUT[13]), .en(ENB), .reset(RST));  // open: Qn, preset
  D_Flip_Flop_part d_ff_16 (.clk(CLK), .D(IN[18]), .Q(OUT[18]), .en(ENB), .reset(RST));  // open: Qn, preset
  D_Flip_Flop_part d_ff_17 (.clk(CLK), .D(IN[4]), .Q(OUT[4]), .en(ENB), .reset(RST));  // open: Qn, preset
  D_Flip_Flop_part d_ff_18 (.clk(CLK), .D(IN[9]), .Q(OUT[9]), .en(ENB), .reset(RST));  // open: Qn, preset
  D_Flip_Flop_part d_ff_19 (.clk(CLK), .D(IN[14]), .Q(OUT[14]), .en(ENB), .reset(RST));  // open: Qn, preset
  D_Flip_Flop_part d_ff_20 (.clk(CLK), .D(IN[19]), .Q(OUT[19]), .en(ENB), .reset(RST));  // open: Qn, preset

  // Notes on the sheet:
  //   We preferred to use built-in D Flip-Flops to prevent getting errors related to Logisim. I would like to point out that our D Flip-Flop operates exactly the same way to the built-in one.
endmodule

module Register_File (
  input  [19:0] IN,
  input  CLK,
  input  LENB,
  input  [3:0] LADDR,
  input  R2ENB,
  input  [3:0] R2ADDR,
  input  R1ENB,
  input  [3:0] R1ADDR,
  input  RST,
  output [19:0] OUT1,
  output [19:0] OUT2
);

  wire decoder_1_out0, decoder_1_out1, decoder_1_out2, decoder_1_out3, decoder_1_out4, decoder_1_out5,
       decoder_1_out6, decoder_1_out7, decoder_1_out8, decoder_1_out9, decoder_1_out10, decoder_1_out11,
       decoder_1_out12, decoder_1_out13, decoder_1_out14, decoder_1_out15;
  wire [19:0] register_1_out, register_2_out, register_3_out, register_4_out, register_5_out, register_6_out,
       register_7_out, register_8_out, register_9_out, register_10_out, register_11_out, register_12_out,
       register_13_out, register_14_out, register_15_out, register_16_out;

  Decoder #(.select(4), .disabled(0)) decoder_1 (
    .out0(decoder_1_out0), .out1(decoder_1_out1), .out2(decoder_1_out2), .out3(decoder_1_out3),
    .out4(decoder_1_out4), .out5(decoder_1_out5), .out6(decoder_1_out6), .out7(decoder_1_out7),
    .out8(decoder_1_out8), .out9(decoder_1_out9), .out10(decoder_1_out10), .out11(decoder_1_out11),
    .out12(decoder_1_out12), .out13(decoder_1_out13), .out14(decoder_1_out14), .out15(decoder_1_out15),
    .sel(LADDR), .en(LENB));
  Register register_1 (.CLK(CLK), .IN(IN), .ENB(decoder_1_out0), .RST(RST), .OUT(register_1_out));
  Register register_2 (.CLK(CLK), .IN(IN), .ENB(decoder_1_out4), .RST(RST), .OUT(register_2_out));
  Register register_3 (.CLK(CLK), .IN(IN), .ENB(decoder_1_out8), .RST(RST), .OUT(register_3_out));
  Register register_4 (.CLK(CLK), .IN(IN), .ENB(decoder_1_out12), .RST(RST), .OUT(register_4_out));
  Register register_5 (.CLK(CLK), .IN(IN), .ENB(decoder_1_out1), .RST(RST), .OUT(register_5_out));
  Register register_6 (.CLK(CLK), .IN(IN), .ENB(decoder_1_out5), .RST(RST), .OUT(register_6_out));
  Register register_7 (.CLK(CLK), .IN(IN), .ENB(decoder_1_out9), .RST(RST), .OUT(register_7_out));
  Register register_8 (.CLK(CLK), .IN(IN), .ENB(decoder_1_out13), .RST(RST), .OUT(register_8_out));
  Register register_9 (.CLK(CLK), .IN(IN), .ENB(decoder_1_out2), .RST(RST), .OUT(register_9_out));
  Register register_10 (.CLK(CLK), .IN(IN), .ENB(decoder_1_out6), .RST(RST), .OUT(register_10_out));
  Register register_11 (.CLK(CLK), .IN(IN), .ENB(decoder_1_out10), .RST(RST), .OUT(register_11_out));
  Register register_12 (.CLK(CLK), .IN(IN), .ENB(decoder_1_out14), .RST(RST), .OUT(register_12_out));
  Register register_13 (.CLK(CLK), .IN(IN), .ENB(decoder_1_out3), .RST(RST), .OUT(register_13_out));
  Register register_14 (.CLK(CLK), .IN(IN), .ENB(decoder_1_out7), .RST(RST), .OUT(register_14_out));
  Register register_15 (.CLK(CLK), .IN(IN), .ENB(decoder_1_out11), .RST(RST), .OUT(register_15_out));
  Register register_16 (.CLK(CLK), .IN(IN), .ENB(decoder_1_out15), .RST(RST), .OUT(register_16_out));
  Multiplexer #(.select(4), .width(20), .disabled(0)) multiplexer_1 (
    .in0(register_1_out), .in1(register_5_out), .in2(register_9_out), .in3(register_13_out),
    .in4(register_2_out), .in5(register_6_out), .in6(register_10_out), .in7(register_14_out),
    .in8(register_3_out), .in9(register_7_out), .in10(register_11_out), .in11(register_15_out),
    .in12(register_4_out), .in13(register_8_out), .in14(register_12_out), .in15(register_16_out), .out(OUT1),
    .sel(R1ADDR), .en(R1ENB));
  Multiplexer #(.select(4), .width(20), .disabled(0)) multiplexer_2 (
    .in0(register_1_out), .in1(register_5_out), .in2(register_9_out), .in3(register_13_out),
    .in4(register_2_out), .in5(register_6_out), .in6(register_10_out), .in7(register_14_out),
    .in8(register_3_out), .in9(register_7_out), .in10(register_11_out), .in11(register_15_out),
    .in12(register_4_out), .in13(register_8_out), .in14(register_12_out), .in15(register_16_out), .out(OUT2),
    .sel(R2ADDR), .en(R2ENB));
endmodule

// MAR
module Address_Register (
  input  CLK,
  input  [19:0] IN,
  input  ENB,
  input  RST,
  input  RD,
  output [9:0] OUT
);

  wire [9:0] d_ff_1_q;

  D_Flip_Flop_part d_ff_1 (.clk(CLK), .D(IN[0]), .Q(d_ff_1_q[0]), .en(ENB), .reset(RST));  // open: Qn, preset
  D_Flip_Flop_part d_ff_2 (.clk(CLK), .D(IN[5]), .Q(d_ff_1_q[5]), .en(ENB), .reset(RST));  // open: Qn, preset
  D_Flip_Flop_part d_ff_3 (.clk(CLK), .D(IN[1]), .Q(d_ff_1_q[1]), .en(ENB), .reset(RST));  // open: Qn, preset
  D_Flip_Flop_part d_ff_4 (.clk(CLK), .D(IN[6]), .Q(d_ff_1_q[6]), .en(ENB), .reset(RST));  // open: Qn, preset
  D_Flip_Flop_part d_ff_5 (.clk(CLK), .D(IN[2]), .Q(d_ff_1_q[2]), .en(ENB), .reset(RST));  // open: Qn, preset
  D_Flip_Flop_part d_ff_6 (.clk(CLK), .D(IN[7]), .Q(d_ff_1_q[7]), .en(ENB), .reset(RST));  // open: Qn, preset
  D_Flip_Flop_part d_ff_7 (.clk(CLK), .D(IN[3]), .Q(d_ff_1_q[3]), .en(ENB), .reset(RST));  // open: Qn, preset
  D_Flip_Flop_part d_ff_8 (.clk(CLK), .D(IN[8]), .Q(d_ff_1_q[8]), .en(ENB), .reset(RST));  // open: Qn, preset
  D_Flip_Flop_part d_ff_9 (.clk(CLK), .D(IN[4]), .Q(d_ff_1_q[4]), .en(ENB), .reset(RST));  // open: Qn, preset
  D_Flip_Flop_part d_ff_10 (.clk(CLK), .D(IN[9]), .Q(d_ff_1_q[9]), .en(ENB), .reset(RST));  // open: Qn, preset
  assign OUT = RD ? d_ff_1_q : 10'bz;  // Controlled_Buffer controlled_buffer_1
endmodule

module ALU (
  input  [19:0] IN1,
  input  RENB,
  input  [19:0] IN2,
  input  [2:0] OP,
  output [19:0] OUT,
  output Zero,
  output Carry,
  output Overflow
);

  wire adder_subtractor_1_carry, adder_subtractor_1_overflow, nor_1_out, not_1_out;
  wire [19:0] adder_subtractor_1_sum, and_1_out, multiplexer_1_out, or_1_out, xor_1_out;

  Adder_Subtractor adder_subtractor_1 (
    .IN1(IN1), .IN2(IN2), .OP(OP[2]), .SUM(adder_subtractor_1_sum), .Carry(adder_subtractor_1_carry),
    .Overflow(adder_subtractor_1_overflow));
  assign xor_1_out = IN1 ^ IN2;  // XOR_Gate xor_1, 20 bits wide
  assign and_1_out = IN1 & IN2;  // AND_Gate and_1, 20 bits wide
  assign or_1_out = IN1 | IN2;  // OR_Gate or_1, 20 bits wide
  Multiplexer #(.select(2), .width(20), .enable("false")) multiplexer_1 (
    .in0(xor_1_out), .in1(and_1_out), .in2(or_1_out), .in3(adder_subtractor_1_sum), .out(multiplexer_1_out),
    .sel(OP[1:0]));
  assign OUT = RENB ? multiplexer_1_out : 20'bz;  // Controlled_Buffer controlled_buffer_1
  not not_1 (not_1_out, RENB);
  nor nor_1 (nor_1_out, multiplexer_1_out[0], multiplexer_1_out[1], multiplexer_1_out[2], multiplexer_1_out[3], multiplexer_1_out[4], multiplexer_1_out[5], multiplexer_1_out[6], multiplexer_1_out[7], multiplexer_1_out[8], multiplexer_1_out[9], multiplexer_1_out[10], multiplexer_1_out[11], multiplexer_1_out[12], multiplexer_1_out[13], multiplexer_1_out[14], multiplexer_1_out[15], multiplexer_1_out[16], multiplexer_1_out[17], multiplexer_1_out[18], multiplexer_1_out[19]);
  D_Flip_Flop_part #(.trigger("low")) d_ff_1 (.clk(not_1_out), .D(nor_1_out), .Q(Zero));  // open: Qn, preset, en, reset
  D_Flip_Flop_part #(.trigger("low")) d_ff_2 (
    .clk(not_1_out), .D(adder_subtractor_1_carry), .Q(Carry));  // open: Qn, preset, en, reset
  D_Flip_Flop_part #(.trigger("low")) d_ff_3 (
    .clk(not_1_out), .D(adder_subtractor_1_overflow), .Q(Overflow));  // open: Qn, preset, en, reset

  // Notes on the sheet:
  //   00    XOR
  //   01    AND
  //   10    OR
  //   0 11    ADD
  //   1 11    SUB
endmodule

module Sign_Extender (
  input  [6:0] IN,
  output [19:0] OUT
);


  assign OUT = {{14{IN[6]}}, IN[5:0]};
endmodule

module Adder_Subtractor (
  input  OP,
  input  [19:0] IN1,
  input  [19:0] IN2,
  output [19:0] SUM,
  output Carry,
  output Overflow
);

  wire and_1_out, and_2_out, and_3_out, and_4_out, fulladder_1_cout, fulladder_2_cout, fulladder_3_cout,
       fulladder_5_cout, fulladder_6_cout, fulladder_7_cout, fulladder_8_cout, fulladder_9_cout,
       fulladder_10_cout, fulladder_11_cout, fulladder_12_cout, fulladder_13_cout, fulladder_14_cout,
       fulladder_15_cout, fulladder_16_cout, fulladder_17_cout, fulladder_18_cout, fulladder_19_cout,
       fulladder_20_cout, xor_1_out, xor_2_out, xor_3_out, xor_4_out, xor_5_out, xor_6_out, xor_7_out,
       xor_8_out, xor_9_out, xor_10_out, xor_11_out, xor_12_out, xor_13_out, xor_14_out, xor_15_out,
       xor_16_out, xor_17_out, xor_18_out, xor_19_out, xor_20_out;

  xor xor_1 (xor_1_out, IN2[4], OP);
  FullAdder fulladder_1 (.IN1(IN1[4]), .IN2(xor_1_out), .CIN(fulladder_5_cout), .COUT(fulladder_1_cout), .SUM(SUM[4]));
  xor xor_2 (xor_2_out, IN2[9], OP);
  FullAdder fulladder_2 (.IN1(IN1[9]), .IN2(xor_2_out), .CIN(fulladder_6_cout), .COUT(fulladder_2_cout), .SUM(SUM[9]));
  xor xor_3 (xor_3_out, IN2[14], OP);
  FullAdder fulladder_3 (
    .IN1(IN1[14]), .IN2(xor_3_out), .CIN(fulladder_7_cout), .COUT(fulladder_3_cout), .SUM(SUM[14]));
  xor xor_4 (xor_4_out, IN2[19], OP);
  FullAdder fulladder_4 (.IN1(IN1[19]), .IN2(xor_4_out), .CIN(fulladder_8_cout), .COUT(Carry), .SUM(SUM[19]));
  xor xor_5 (xor_5_out, IN2[3], OP);
  FullAdder fulladder_5 (.IN1(IN1[3]), .IN2(xor_5_out), .CIN(fulladder_9_cout), .COUT(fulladder_5_cout), .SUM(SUM[3]));
  xor xor_6 (xor_6_out, IN2[8], OP);
  FullAdder fulladder_6 (.IN1(IN1[8]), .IN2(xor_6_out), .CIN(fulladder_10_cout), .COUT(fulladder_6_cout), .SUM(SUM[8]));
  xor xor_7 (xor_7_out, IN2[13], OP);
  FullAdder fulladder_7 (
    .IN1(IN1[13]), .IN2(xor_7_out), .CIN(fulladder_11_cout), .COUT(fulladder_7_cout), .SUM(SUM[13]));
  xor xor_8 (xor_8_out, IN2[18], OP);
  FullAdder fulladder_8 (
    .IN1(IN1[18]), .IN2(xor_8_out), .CIN(fulladder_12_cout), .COUT(fulladder_8_cout), .SUM(SUM[18]));
  xor xor_9 (xor_9_out, IN2[2], OP);
  FullAdder fulladder_9 (.IN1(IN1[2]), .IN2(xor_9_out), .CIN(fulladder_13_cout), .COUT(fulladder_9_cout), .SUM(SUM[2]));
  xor xor_10 (xor_10_out, IN2[7], OP);
  FullAdder fulladder_10 (
    .IN1(IN1[7]), .IN2(xor_10_out), .CIN(fulladder_14_cout), .COUT(fulladder_10_cout), .SUM(SUM[7]));
  xor xor_11 (xor_11_out, IN2[12], OP);
  FullAdder fulladder_11 (
    .IN1(IN1[12]), .IN2(xor_11_out), .CIN(fulladder_15_cout), .COUT(fulladder_11_cout), .SUM(SUM[12]));
  xor xor_12 (xor_12_out, IN2[17], OP);
  FullAdder fulladder_12 (
    .IN1(IN1[17]), .IN2(xor_12_out), .CIN(fulladder_16_cout), .COUT(fulladder_12_cout), .SUM(SUM[17]));
  xor xor_13 (xor_13_out, IN2[1], OP);
  FullAdder fulladder_13 (
    .IN1(IN1[1]), .IN2(xor_13_out), .CIN(fulladder_17_cout), .COUT(fulladder_13_cout), .SUM(SUM[1]));
  xor xor_14 (xor_14_out, IN2[6], OP);
  FullAdder fulladder_14 (
    .IN1(IN1[6]), .IN2(xor_14_out), .CIN(fulladder_18_cout), .COUT(fulladder_14_cout), .SUM(SUM[6]));
  xor xor_15 (xor_15_out, IN2[11], OP);
  FullAdder fulladder_15 (
    .IN1(IN1[11]), .IN2(xor_15_out), .CIN(fulladder_19_cout), .COUT(fulladder_15_cout), .SUM(SUM[11]));
  xor xor_16 (xor_16_out, IN2[16], OP);
  FullAdder fulladder_16 (
    .IN1(IN1[16]), .IN2(xor_16_out), .CIN(fulladder_20_cout), .COUT(fulladder_16_cout), .SUM(SUM[16]));
  xor xor_17 (xor_17_out, IN2[0], OP);
  FullAdder fulladder_17 (.IN1(IN1[0]), .IN2(xor_17_out), .CIN(OP), .COUT(fulladder_17_cout), .SUM(SUM[0]));
  xor xor_18 (xor_18_out, IN2[5], OP);
  FullAdder fulladder_18 (
    .IN1(IN1[5]), .IN2(xor_18_out), .CIN(fulladder_1_cout), .COUT(fulladder_18_cout), .SUM(SUM[5]));
  xor xor_19 (xor_19_out, IN2[10], OP);
  FullAdder fulladder_19 (
    .IN1(IN1[10]), .IN2(xor_19_out), .CIN(fulladder_2_cout), .COUT(fulladder_19_cout), .SUM(SUM[10]));
  xor xor_20 (xor_20_out, IN2[15], OP);
  FullAdder fulladder_20 (
    .IN1(IN1[15]), .IN2(xor_20_out), .CIN(fulladder_3_cout), .COUT(fulladder_20_cout), .SUM(SUM[15]));
  and and_1 (and_1_out, SUM[19], ~OP, ~IN2[19], ~IN1[19]);  // AND_Gate
  and and_2 (and_2_out, SUM[19], OP, IN2[19], ~IN1[19]);  // AND_Gate
  and and_3 (and_3_out, ~SUM[19], OP, ~IN2[19], IN1[19]);  // AND_Gate
  and and_4 (and_4_out, ~SUM[19], ~OP, IN2[19], IN1[19]);  // AND_Gate
  or or_1 (Overflow, and_1_out, and_2_out, and_3_out, and_4_out);
endmodule

// PC
module Program_Counter (
  input  LD,
  input  [9:0] ADDR,
  input  INC,
  input  CLK,
  input  RST,
  input  RD,
  output [9:0] out_7
);

  wire and_1_out, not_1_out;
  wire [9:0] counter_1_q;

  not not_1 (not_1_out, LD);
  and and_1 (and_1_out, not_1_out, INC);
  assign out_7 = RD ? counter_1_q : 10'bz;  // Controlled_Buffer controlled_buffer_1
  Counter #(.width(10), .max('h3ff)) counter_1 (
    .load(LD), .D(ADDR), .count(and_1_out), .Q(counter_1_q), .carry(RST), .clk(CLK), .clr(RST));

  // Notes on the sheet:
  //   We're planning to build this counter using JK flip-flops next time.
endmodule

module Address_Extender (
  input  [9:0] IN,
  output [19:0] OUT
);


  assign OUT = {{10{1'b0}}, IN};
endmodule

module SR_Latch (
  input  S,
  input  ENB,
  input  R,
  input  PRE,
  input  CLR,
  output Q,
  output NOT_Q
);

  wire nand_1_out, nand_2_out, not_1_out, not_2_out;

  nand nand_1 (nand_1_out, S, ENB);
  nand nand_2 (nand_2_out, ENB, R);
  not not_1 (not_1_out, PRE);
  nand nand_3 (Q, not_1_out, nand_1_out, NOT_Q);
  nand nand_4 (NOT_Q, Q, nand_2_out, not_2_out);
  not not_2 (not_2_out, CLR);
endmodule

module D_Latch (
  input  ENB,
  input  D,
  input  PRE,
  input  CLR,
  output Q,
  output NOT_Q
);

  wire not_1_out;

  SR_Latch sr_latch_1 (.S(D), .ENB(ENB), .R(not_1_out), .PRE(PRE), .CLR(CLR), .Q(Q), .NOT_Q(NOT_Q));
  not not_1 (not_1_out, D);
endmodule

module D_Flip_Flop (
  input  CLK,
  input  D,
  input  PRE,
  input  ENB,
  input  CLR,
  output Q,
  output NOT_Q
);

  wire and_1_out, d_latch_1_not_q, not_1_out, not_2_out;

  and and_1 (and_1_out, CLK, ENB);
  D_Latch d_latch_1 (.ENB(and_1_out), .D(D), .PRE(PRE), .CLR(CLR), .NOT_Q(d_latch_1_not_q));  // open: Q
  not not_1 (not_1_out, and_1_out);
  not not_2 (not_2_out, d_latch_1_not_q);
  D_Latch d_latch_2 (.ENB(not_1_out), .D(not_2_out), .PRE(PRE), .CLR(CLR), .Q(Q), .NOT_Q(NOT_Q));
endmodule

module Address_Extractor (
  input  [19:0] IN,
  output [9:0] OUT
);


  assign OUT = IN[9:0];
endmodule

module ALUOp (
  input  [3:0] IN,
  output [2:0] OUT
);

  wire and_2_out, and_3_out, and_4_out, and_5_out, and_6_out, and_7_out, and_8_out, not_1_out, not_2_out,
       not_3_out, not_4_out, not_5_out, not_6_out, not_7_out, not_8_out, not_9_out, not_10_out, not_11_out,
       not_12_out, not_13_out, not_14_out, not_15_out, not_16_out, not_17_out, not_18_out, not_19_out,
       not_20_out, not_21_out, not_22_out;

  not not_1 (not_1_out, IN[3]);
  not not_2 (not_2_out, IN[2]);
  not not_3 (not_3_out, IN[0]);
  not not_4 (not_4_out, IN[3]);
  not not_5 (not_5_out, IN[2]);
  not not_6 (not_6_out, IN[1]);
  not not_7 (not_7_out, IN[3]);
  not not_8 (not_8_out, IN[2]);
  not not_9 (not_9_out, IN[0]);
  not not_10 (not_10_out, IN[3]);
  not not_11 (not_11_out, IN[1]);
  not not_12 (not_12_out, IN[0]);
  not not_13 (not_13_out, IN[2]);
  not not_14 (not_14_out, IN[1]);
  not not_15 (not_15_out, IN[0]);
  not not_16 (not_16_out, IN[3]);
  not not_17 (not_17_out, IN[2]);
  not not_18 (not_18_out, IN[3]);
  not not_19 (not_19_out, IN[2]);
  not not_20 (not_20_out, IN[2]);
  not not_21 (not_21_out, IN[1]);
  not not_22 (not_22_out, IN[0]);
  and and_1 (OUT[2], not_1_out, not_2_out, IN[1], not_3_out);
  and and_2 (and_2_out, not_4_out, not_5_out, not_6_out, IN[0]);
  and and_3 (and_3_out, not_7_out, not_8_out, IN[1], not_9_out);
  and and_4 (and_4_out, not_10_out, IN[2], not_11_out, not_12_out);
  and and_5 (and_5_out, IN[3], not_13_out, not_14_out, not_15_out);
  and and_6 (and_6_out, not_16_out, not_17_out, IN[0]);
  and and_7 (and_7_out, not_18_out, not_19_out, IN[1]);
  and and_8 (and_8_out, IN[3], not_20_out, not_21_out, not_22_out);
  or or_1 (OUT[1], and_2_out, and_3_out, and_4_out, and_5_out);
  or or_2 (OUT[0], and_6_out, and_7_out, and_8_out);
endmodule

module MemOpDetector (
  input  [3:0] IN,
  output OUT
);

  and and_1 (OUT, ~IN[3], IN[2], IN[1], IN[0]);  // AND_Gate
endmodule

module RdRegister (
  input  CLK,
  input  [19:0] IN,
  input  WR,
  input  RST,
  input  RD,
  output [19:0] OUT
);

  wire [19:0] register_1_out;

  Register register_1 (.CLK(CLK), .IN(IN), .ENB(WR), .RST(RST), .OUT(register_1_out));
  assign OUT = RD ? register_1_out : 20'bz;  // Controlled_Buffer controlled_buffer_1
endmodule

module Layout_Select (
  input  [3:0] IN,
  output [1:0] OUT
);

  wire and_1_out, and_2_out, not_1_out, not_2_out, not_3_out, not_4_out;

  not not_1 (not_1_out, IN[2]);
  not not_2 (not_2_out, IN[1]);
  not not_3 (not_3_out, IN[0]);
  not not_4 (not_4_out, IN[3]);
  and and_1 (and_1_out, IN[3], not_1_out, IN[1], IN[0]);
  and and_2 (and_2_out, IN[3], IN[2], not_2_out, not_3_out);
  and and_3 (OUT[0], not_4_out, IN[2], IN[1], IN[0]);
  or or_1 (OUT[1], and_1_out, and_2_out);
endmodule

module PC_Controller (
  input  CLK,
  input  [3:0] IN,
  output PCInc,
  output PCWrt,
  output PCRst,
  output PCRd
);

  wire and_2_out, and_3_out, and_4_out, and_5_out, and_6_out, and_7_out, and_8_out, and_9_out, and_10_out,
       and_11_out, and_12_out, d_ff_1_q, d_ff_2_q, not_1_out, not_2_out, not_3_out, not_4_out, not_5_out,
       not_6_out, not_7_out, not_8_out, not_9_out, not_10_out, not_11_out, not_12_out, not_13_out,
       not_14_out, not_15_out, not_16_out, not_17_out, not_18_out, not_19_out, not_20_out, not_21_out,
       not_22_out, not_23_out, not_24_out, not_25_out, not_26_out, not_27_out, not_28_out, not_29_out,
       not_30_out, xor_1_out;

  xor xor_1 (xor_1_out, d_ff_1_q, d_ff_2_q);
  not not_1 (not_1_out, d_ff_2_q);
  not not_2 (not_2_out, d_ff_1_q);
  not not_3 (not_3_out, d_ff_2_q);
  not not_4 (not_4_out, d_ff_1_q);
  not not_5 (not_5_out, IN[2]);
  not not_6 (not_6_out, IN[1]);
  not not_7 (not_7_out, IN[0]);
  not not_8 (not_8_out, d_ff_2_q);
  not not_9 (not_9_out, IN[2]);
  not not_10 (not_10_out, d_ff_2_q);
  not not_11 (not_11_out, IN[1]);
  not not_12 (not_12_out, IN[0]);
  not not_13 (not_13_out, d_ff_1_q);
  not not_14 (not_14_out, d_ff_2_q);
  not not_15 (not_15_out, d_ff_1_q);
  not not_16 (not_16_out, IN[3]);
  not not_17 (not_17_out, d_ff_1_q);
  not not_18 (not_18_out, IN[1]);
  not not_19 (not_19_out, IN[0]);
  not not_20 (not_20_out, d_ff_1_q);
  not not_21 (not_21_out, IN[2]);
  not not_22 (not_22_out, d_ff_2_q);
  not not_23 (not_23_out, IN[3]);
  not not_24 (not_24_out, IN[3]);
  not not_25 (not_25_out, IN[0]);
  not not_26 (not_26_out, d_ff_2_q);
  not not_27 (not_27_out, IN[2]);
  not not_28 (not_28_out, d_ff_2_q);
  not not_29 (not_29_out, IN[1]);
  not not_30 (not_30_out, IN[0]);
  and and_1 (PCInc, not_2_out, not_3_out);
  and and_2 (and_2_out, not_4_out, d_ff_2_q, IN[3], not_5_out, not_6_out, not_7_out);
  and and_3 (and_3_out, d_ff_1_q, not_8_out, IN[3], not_9_out, IN[1], IN[0]);
  and and_4 (and_4_out, d_ff_1_q, not_10_out, IN[3], IN[2], not_11_out, not_12_out);
  and and_5 (and_5_out, not_13_out, not_14_out);
  and and_6 (and_6_out, not_15_out, not_16_out);
  and and_7 (and_7_out, not_17_out, not_18_out, not_19_out);
  and and_8 (and_8_out, not_20_out, not_21_out, IN[1], IN[0]);
  and and_9 (and_9_out, not_22_out, not_23_out, IN[2], IN[1]);
  and and_10 (and_10_out, not_24_out, IN[2], IN[1], not_25_out);
  and and_11 (and_11_out, not_26_out, IN[3], not_27_out, IN[1], IN[0]);
  and and_12 (and_12_out, not_28_out, IN[3], IN[2], not_29_out, not_30_out);
  or or_1 (PCWrt, and_2_out, and_3_out, and_4_out);
  or or_2 (PCRd, and_5_out, and_6_out, and_7_out, and_8_out, and_9_out, and_10_out, and_11_out, and_12_out);
  D_Flip_Flop_part d_ff_1 (.clk(CLK), .D(xor_1_out), .Q(d_ff_1_q));  // open: Qn, preset, en, reset
  D_Flip_Flop_part d_ff_2 (.clk(CLK), .D(not_1_out), .Q(d_ff_2_q));  // open: Qn, preset, en, reset

  assign PCRst = 1'b0;
endmodule

module MAR_Controller (
  input  CLK,
  input  [3:0] IN,
  output MARWrt,
  output MARRst,
  output MARRd
);

  wire d_ff_1_q, d_ff_2_q, not_1_out, not_2_out, not_3_out, not_4_out, not_5_out, xor_1_out;

  xor xor_1 (xor_1_out, d_ff_1_q, d_ff_2_q);
  not not_1 (not_1_out, d_ff_2_q);
  not not_2 (not_2_out, d_ff_1_q);
  not not_3 (not_3_out, IN[3]);
  not not_4 (not_4_out, d_ff_2_q);
  not not_5 (not_5_out, IN[3]);
  and and_1 (MARWrt, not_2_out, d_ff_2_q, not_3_out, IN[2], IN[1]);
  and and_2 (MARRd, d_ff_1_q, not_4_out, not_5_out, IN[2], IN[1]);
  D_Flip_Flop_part d_ff_1 (.clk(CLK), .D(xor_1_out), .Q(d_ff_1_q));  // open: Qn, preset, en, reset
  D_Flip_Flop_part d_ff_2 (.clk(CLK), .D(not_1_out), .Q(d_ff_2_q));  // open: Qn, preset, en, reset

  assign MARRst = 1'b0;
endmodule

module IM_Controller (
  input  CLK,
  input  [3:0] IN,
  output IMSel
);

  wire and_1_out, and_2_out, and_3_out, and_4_out, and_5_out, and_6_out, and_7_out, and_8_out, and_9_out,
       d_ff_1_q, d_ff_2_q, not_1_out, not_2_out, not_3_out, not_4_out, not_5_out, not_6_out, not_7_out,
       not_8_out, not_9_out, not_10_out, not_11_out, not_12_out, not_13_out, not_14_out, not_15_out,
       not_16_out, not_17_out, not_18_out, not_19_out, not_20_out, not_21_out, not_22_out, not_23_out,
       xor_1_out;

  not not_1 (not_1_out, d_ff_2_q);
  not not_2 (not_2_out, d_ff_1_q);
  not not_3 (not_3_out, d_ff_2_q);
  not not_4 (not_4_out, d_ff_1_q);
  not not_5 (not_5_out, IN[3]);
  not not_6 (not_6_out, IN[1]);
  not not_7 (not_7_out, d_ff_1_q);
  not not_8 (not_8_out, IN[3]);
  not not_9 (not_9_out, IN[0]);
  not not_10 (not_10_out, d_ff_1_q);
  not not_11 (not_11_out, IN[1]);
  not not_12 (not_12_out, IN[0]);
  not not_13 (not_13_out, d_ff_1_q);
  not not_14 (not_14_out, IN[2]);
  not not_15 (not_15_out, d_ff_2_q);
  not not_16 (not_16_out, IN[3]);
  not not_17 (not_17_out, IN[3]);
  not not_18 (not_18_out, IN[0]);
  not not_19 (not_19_out, d_ff_2_q);
  not not_20 (not_20_out, IN[2]);
  not not_21 (not_21_out, d_ff_2_q);
  not not_22 (not_22_out, IN[1]);
  not not_23 (not_23_out, IN[0]);
  xor xor_1 (xor_1_out, d_ff_1_q, d_ff_2_q);
  and and_1 (and_1_out, not_2_out, not_3_out);
  and and_2 (and_2_out, not_4_out, not_5_out, not_6_out);
  and and_3 (and_3_out, not_7_out, not_8_out, not_9_out);
  and and_4 (and_4_out, not_10_out, not_11_out, not_12_out);
  and and_5 (and_5_out, not_13_out, not_14_out, IN[1], IN[0]);
  and and_6 (and_6_out, not_15_out, not_16_out, IN[2], IN[1]);
  and and_7 (and_7_out, not_17_out, IN[2], IN[1], not_18_out);
  and and_8 (and_8_out, not_19_out, IN[3], not_20_out, IN[1], IN[0]);
  and and_9 (and_9_out, not_21_out, IN[3], IN[2], not_22_out, not_23_out);
  D_Flip_Flop_part d_ff_1 (.clk(CLK), .D(xor_1_out), .Q(d_ff_1_q));  // open: Qn, preset, en, reset
  D_Flip_Flop_part d_ff_2 (.clk(CLK), .D(not_1_out), .Q(d_ff_2_q));  // open: Qn, preset, en, reset
  or or_1 (IMSel, and_1_out, and_2_out, and_3_out, and_4_out, and_5_out, and_6_out, and_7_out, and_8_out, and_9_out);
endmodule

module DM_Controller (
  input  CLK,
  input  [3:0] IN,
  output DMWrt,
  output DMSel,
  output DMRd,
  output DMRst
);

  wire and_2_out, and_3_out, and_4_out, and_5_out, d_ff_1_q, d_ff_2_q, not_1_out, not_2_out, not_3_out,
       not_4_out, not_5_out, not_6_out, not_7_out, not_8_out, not_9_out, not_10_out, not_11_out, not_12_out,
       not_13_out, not_14_out, not_15_out, not_16_out, xor_1_out;

  not not_1 (not_1_out, d_ff_2_q);
  not not_2 (not_2_out, d_ff_2_q);
  not not_3 (not_3_out, IN[3]);
  not not_4 (not_4_out, d_ff_1_q);
  not not_5 (not_5_out, IN[3]);
  not not_6 (not_6_out, d_ff_1_q);
  not not_7 (not_7_out, IN[2]);
  not not_8 (not_8_out, IN[1]);
  not not_9 (not_9_out, IN[0]);
  not not_10 (not_10_out, d_ff_2_q);
  not not_11 (not_11_out, IN[3]);
  not not_12 (not_12_out, IN[3]);
  not not_13 (not_13_out, IN[0]);
  not not_14 (not_14_out, d_ff_2_q);
  not not_15 (not_15_out, IN[3]);
  not not_16 (not_16_out, IN[0]);
  xor xor_1 (xor_1_out, d_ff_1_q, d_ff_2_q);
  and and_1 (DMWrt, d_ff_1_q, not_2_out, not_3_out, IN[2], IN[1], IN[0]);
  and and_2 (and_2_out, not_4_out, d_ff_2_q, not_5_out, IN[2], IN[1]);
  and and_3 (and_3_out, not_6_out, d_ff_2_q, IN[3], not_7_out, not_8_out, not_9_out);
  and and_4 (and_4_out, d_ff_1_q, not_10_out, not_11_out, IN[2], IN[1]);
  and and_5 (and_5_out, d_ff_1_q, not_12_out, IN[2], IN[1], not_13_out);
  and and_6 (DMRd, d_ff_1_q, not_14_out, not_15_out, IN[2], IN[1], not_16_out);
  or or_1 (DMSel, and_2_out, and_3_out, and_4_out, and_5_out);
  D_Flip_Flop_part d_ff_1 (.clk(CLK), .D(xor_1_out), .Q(d_ff_1_q));  // open: Qn, preset, en, reset
  D_Flip_Flop_part d_ff_2 (.clk(CLK), .D(not_1_out), .Q(d_ff_2_q));  // open: Qn, preset, en, reset

  assign DMRst = 1'b0;
endmodule

module MDR_Controller (
  input  CLK,
  input  [3:0] IN,
  output MDRWrt,
  output MDRRst,
  output MDRRd
);

  wire and_1_out, and_2_out, and_3_out, and_4_out, d_ff_1_q, d_ff_2_q, not_1_out, not_2_out, not_3_out,
       not_4_out, not_5_out, not_6_out, not_7_out, not_8_out, not_9_out, not_10_out, xor_1_out;

  not not_1 (not_1_out, d_ff_2_q);
  not not_2 (not_2_out, d_ff_1_q);
  not not_3 (not_3_out, IN[3]);
  not not_4 (not_4_out, d_ff_2_q);
  not not_5 (not_5_out, IN[3]);
  not not_6 (not_6_out, IN[0]);
  not not_7 (not_7_out, d_ff_2_q);
  not not_8 (not_8_out, IN[3]);
  not not_9 (not_9_out, IN[3]);
  not not_10 (not_10_out, IN[0]);
  xor xor_1 (xor_1_out, d_ff_1_q, d_ff_2_q);
  and and_1 (and_1_out, not_2_out, d_ff_2_q, not_3_out, IN[2], IN[1], IN[0]);
  or or_1 (MDRWrt, and_1_out, and_2_out);
  and and_2 (and_2_out, d_ff_1_q, not_4_out, not_5_out, IN[2], IN[1], not_6_out);
  and and_3 (and_3_out, d_ff_1_q, not_7_out, not_8_out, IN[2], IN[1], IN[0]);
  or or_2 (MDRRd, and_3_out, and_4_out);
  and and_4 (and_4_out, d_ff_1_q, d_ff_2_q, not_9_out, IN[2], IN[1], not_10_out);
  D_Flip_Flop_part d_ff_1 (.clk(CLK), .D(xor_1_out), .Q(d_ff_1_q));  // open: Qn, preset, en, reset
  D_Flip_Flop_part d_ff_2 (.clk(CLK), .D(not_1_out), .Q(d_ff_2_q));  // open: Qn, preset, en, reset

  assign MDRRst = 1'b0;
endmodule

module Register_File_Controller (
  input  CLK,
  input  [3:0] IN,
  output RegWrt,
  output Reg2Rd,
  output Reg1Rd,
  output RegRst
);

  wire and_1_out, and_2_out, and_3_out, and_4_out, and_5_out, and_6_out, and_7_out, and_8_out, and_9_out,
       and_10_out, and_11_out, and_12_out, d_ff_1_q, d_ff_2_q, not_1_out, not_2_out, not_3_out, not_4_out,
       not_5_out, not_6_out, not_7_out, not_8_out, not_9_out, not_10_out, not_11_out, not_12_out, not_13_out,
       not_14_out, not_15_out, not_16_out, not_17_out, not_18_out, not_19_out, not_20_out, not_21_out,
       not_22_out, not_23_out, not_24_out, not_25_out, not_26_out, not_27_out, not_28_out, not_29_out,
       not_30_out, not_31_out, not_32_out, not_33_out, xor_1_out;

  xor xor_1 (xor_1_out, d_ff_1_q, d_ff_2_q);
  not not_1 (not_1_out, d_ff_2_q);
  not not_2 (not_2_out, d_ff_1_q);
  not not_3 (not_3_out, IN[3]);
  not not_4 (not_4_out, IN[2]);
  not not_5 (not_5_out, d_ff_1_q);
  not not_6 (not_6_out, IN[3]);
  not not_7 (not_7_out, IN[2]);
  not not_8 (not_8_out, d_ff_1_q);
  not not_9 (not_9_out, IN[3]);
  not not_10 (not_10_out, IN[1]);
  not not_11 (not_11_out, IN[3]);
  not not_12 (not_12_out, IN[0]);
  not not_13 (not_13_out, d_ff_1_q);
  not not_14 (not_14_out, IN[3]);
  not not_15 (not_15_out, IN[1]);
  not not_16 (not_16_out, d_ff_1_q);
  not not_17 (not_17_out, IN[3]);
  not not_18 (not_18_out, IN[2]);
  not not_19 (not_19_out, d_ff_1_q);
  not not_20 (not_20_out, IN[2]);
  not not_21 (not_21_out, d_ff_1_q);
  not not_22 (not_22_out, IN[1]);
  not not_23 (not_23_out, IN[0]);
  not not_24 (not_24_out, d_ff_1_q);
  not not_25 (not_25_out, IN[3]);
  not not_26 (not_26_out, d_ff_1_q);
  not not_27 (not_27_out, IN[3]);
  not not_28 (not_28_out, IN[2]);
  not not_29 (not_29_out, d_ff_1_q);
  not not_30 (not_30_out, IN[2]);
  not not_31 (not_31_out, d_ff_1_q);
  not not_32 (not_32_out, IN[1]);
  not not_33 (not_33_out, IN[0]);
  and and_1 (and_1_out, not_2_out, d_ff_2_q, not_3_out, not_4_out, IN[0]);
  and and_2 (and_2_out, not_5_out, d_ff_2_q, not_6_out, not_7_out, IN[1]);
  and and_3 (and_3_out, not_8_out, d_ff_2_q, not_9_out, IN[2], not_10_out);
  and and_4 (and_4_out, d_ff_1_q, d_ff_2_q, not_11_out, IN[2], IN[1], not_12_out);
  and and_5 (and_5_out, not_13_out, d_ff_2_q, not_14_out, not_15_out, IN[0]);
  and and_6 (and_6_out, not_16_out, d_ff_2_q, not_17_out, not_18_out, IN[1]);
  and and_7 (and_7_out, not_19_out, d_ff_2_q, not_20_out, IN[1], IN[0]);
  and and_8 (and_8_out, not_21_out, d_ff_2_q, IN[2], not_22_out, not_23_out);
  and and_9 (and_9_out, not_24_out, d_ff_2_q, not_25_out, IN[0]);
  and and_10 (and_10_out, not_26_out, d_ff_2_q, not_27_out, not_28_out, IN[1]);
  and and_11 (and_11_out, not_29_out, d_ff_2_q, not_30_out, IN[1], IN[0]);
  and and_12 (and_12_out, not_31_out, d_ff_2_q, IN[2], not_32_out, not_33_out);
  or or_1 (RegWrt, and_1_out, and_2_out, and_3_out, and_4_out);
  or or_2 (Reg2Rd, and_5_out, and_6_out, and_7_out, and_8_out);
  or or_3 (Reg1Rd, and_9_out, and_10_out, and_11_out, and_12_out);
  D_Flip_Flop_part d_ff_1 (.clk(CLK), .D(xor_1_out), .Q(d_ff_1_q));  // open: Qn, preset, en, reset
  D_Flip_Flop_part d_ff_2 (.clk(CLK), .D(not_1_out), .Q(d_ff_2_q));  // open: Qn, preset, en, reset

  assign RegRst = 1'b0;
endmodule

module Jump_Controller (
  input  CLK,
  input  [3:0] IN,
  output JumpRd
);

  wire d_ff_1_q, d_ff_2_q, not_1_out, not_2_out, not_3_out, not_4_out, not_5_out, xor_1_out;

  not not_1 (not_1_out, d_ff_2_q);
  not not_2 (not_2_out, d_ff_1_q);
  not not_3 (not_3_out, IN[2]);
  not not_4 (not_4_out, IN[1]);
  not not_5 (not_5_out, IN[0]);
  xor xor_1 (xor_1_out, d_ff_1_q, d_ff_2_q);
  D_Flip_Flop_part d_ff_1 (.clk(CLK), .D(xor_1_out), .Q(d_ff_1_q));  // open: Qn, preset, en, reset
  D_Flip_Flop_part d_ff_2 (.clk(CLK), .D(not_1_out), .Q(d_ff_2_q));  // open: Qn, preset, en, reset
  and and_1 (JumpRd, not_2_out, d_ff_2_q, IN[3], not_3_out, not_4_out, not_5_out);
endmodule

module ALU_Controller (
  input  CLK,
  input  [3:0] IN,
  output ALURd
);

  wire and_1_out, and_2_out, and_3_out, and_4_out, and_5_out, d_ff_1_q, d_ff_2_q, not_1_out, not_2_out,
       not_3_out, not_4_out, not_5_out, not_6_out, not_7_out, not_8_out, not_9_out, not_10_out, not_11_out,
       not_12_out, not_13_out, not_14_out, not_15_out, xor_1_out;

  xor xor_1 (xor_1_out, d_ff_1_q, d_ff_2_q);
  not not_1 (not_1_out, d_ff_2_q);
  not not_2 (not_2_out, d_ff_1_q);
  not not_3 (not_3_out, IN[3]);
  not not_4 (not_4_out, IN[2]);
  not not_5 (not_5_out, d_ff_1_q);
  not not_6 (not_6_out, IN[3]);
  not not_7 (not_7_out, IN[2]);
  not not_8 (not_8_out, d_ff_1_q);
  not not_9 (not_9_out, IN[2]);
  not not_10 (not_10_out, d_ff_1_q);
  not not_11 (not_11_out, IN[3]);
  not not_12 (not_12_out, IN[1]);
  not not_13 (not_13_out, d_ff_1_q);
  not not_14 (not_14_out, IN[1]);
  not not_15 (not_15_out, IN[0]);
  and and_1 (and_1_out, not_2_out, d_ff_2_q, not_3_out, not_4_out, IN[0]);
  and and_2 (and_2_out, not_5_out, d_ff_2_q, not_6_out, not_7_out, IN[1]);
  and and_3 (and_3_out, not_8_out, d_ff_2_q, not_9_out, IN[1], IN[0]);
  and and_4 (and_4_out, not_10_out, d_ff_2_q, not_11_out, IN[2], not_12_out);
  and and_5 (and_5_out, not_13_out, d_ff_2_q, IN[3], not_14_out, not_15_out);
  or or_1 (ALURd, and_1_out, and_2_out, and_3_out, and_4_out, and_5_out);
  D_Flip_Flop_part d_ff_1 (.clk(CLK), .D(xor_1_out), .Q(d_ff_1_q));  // open: Qn, preset, en, reset
  D_Flip_Flop_part d_ff_2 (.clk(CLK), .D(not_1_out), .Q(d_ff_2_q));  // open: Qn, preset, en, reset
endmodule

module NOOp_Controller (
  input  CLK,
  input  [3:0] IN,
  output NOOp
);

  wire d_ff_1_q, d_ff_2_q, not_1_out, not_2_out, not_3_out, not_4_out, not_5_out, not_6_out, xor_1_out;

  not not_1 (not_1_out, d_ff_2_q);
  not not_2 (not_2_out, d_ff_1_q);
  not not_3 (not_3_out, IN[3]);
  not not_4 (not_4_out, IN[2]);
  not not_5 (not_5_out, IN[1]);
  not not_6 (not_6_out, IN[0]);
  xor xor_1 (xor_1_out, d_ff_1_q, d_ff_2_q);
  and and_1 (NOOp, not_2_out, d_ff_2_q, not_3_out, not_4_out, not_5_out, not_6_out);
  D_Flip_Flop_part d_ff_1 (.clk(CLK), .D(xor_1_out), .Q(d_ff_1_q));  // open: Qn, preset, en, reset
  D_Flip_Flop_part d_ff_2 (.clk(CLK), .D(not_1_out), .Q(d_ff_2_q));  // open: Qn, preset, en, reset
endmodule

module IR_Controller (
  input  CLK,
  input  [3:0] IN,
  output IRWrt,
  output IRRst
);

  wire d_ff_1_q, d_ff_2_q, not_1_out, not_2_out, not_3_out, xor_1_out;

  xor xor_1 (xor_1_out, d_ff_1_q, d_ff_2_q);
  not not_1 (not_1_out, d_ff_2_q);
  not not_2 (not_2_out, d_ff_1_q);
  not not_3 (not_3_out, d_ff_2_q);
  D_Flip_Flop_part d_ff_1 (.clk(CLK), .D(xor_1_out), .Q(d_ff_1_q));  // open: Qn, preset, en, reset
  D_Flip_Flop_part d_ff_2 (.clk(CLK), .D(not_1_out), .Q(d_ff_2_q));  // open: Qn, preset, en, reset
  and and_1 (IRWrt, not_2_out, not_3_out);

  assign IRRst = 1'b0;
endmodule

module Control_Unit (
  input  CLK,
  input  [3:0] Opcode,
  output out_3,
  output out_4,
  output out_5,
  output out_6,
  output out_7,
  output out_8,
  output out_9,
  output out_10,
  output out_11,
  output out_12,
  output out_13,
  output out_14,
  output out_15,
  output out_16,
  output out_17,
  output out_18,
  output out_19,
  output out_20,
  output out_21,
  output out_22,
  output out_23,
  output out_24,
  output out_25,
  output out_26,
  output out_27
);

  PC_Controller pc_controller_1 (.IN(Opcode), .CLK(CLK), .PCInc(out_3), .PCWrt(out_4), .PCRst(out_5), .PCRd(out_6));
  MAR_Controller mar_controller_1 (.IN(Opcode), .CLK(CLK), .MARWrt(out_7), .MARRst(out_8), .MARRd(out_9));
  IM_Controller im_controller_1 (.IN(Opcode), .CLK(CLK), .IMSel(out_10));
  DM_Controller dm_controller_1 (.IN(Opcode), .CLK(CLK), .DMWrt(out_11), .DMSel(out_12), .DMRd(out_13), .DMRst(out_14));
  MDR_Controller mdr_controller_1 (.IN(Opcode), .CLK(CLK), .MDRWrt(out_15), .MDRRst(out_16), .MDRRd(out_17));
  Register_File_Controller register_file_controller_1 (
    .IN(Opcode), .CLK(CLK), .RegWrt(out_18), .Reg2Rd(out_19), .Reg1Rd(out_20), .RegRst(out_21));
  Jump_Controller jump_controller_1 (.IN(Opcode), .CLK(CLK), .JumpRd(out_22));
  ALU_Controller alu_controller_1 (.IN(Opcode), .CLK(CLK), .ALURd(out_23));
  NOOp_Controller noop_controller_1 (.IN(Opcode), .CLK(CLK), .NOOp(out_24));
  IR_Controller ir_controller_1 (.IN(Opcode), .CLK(CLK), .IRWrt(out_25), .IRRst(out_26));
  Conditional_Jump_Controller conditional_jump_controller_1 (.IN(Opcode), .CondJump(out_27), .CLK(CLK));
endmodule

module Conditional_Jump_Controller (
  input  CLK,
  input  [3:0] IN,
  output CondJump
);

  wire and_1_out, and_2_out, d_ff_1_q, d_ff_2_q, not_1_out, not_2_out, not_3_out, not_4_out, not_5_out,
       not_6_out, xor_1_out;

  xor xor_1 (xor_1_out, d_ff_1_q, d_ff_2_q);
  not not_1 (not_1_out, d_ff_2_q);
  not not_2 (not_2_out, d_ff_2_q);
  not not_3 (not_3_out, IN[2]);
  not not_4 (not_4_out, d_ff_2_q);
  not not_5 (not_5_out, IN[1]);
  not not_6 (not_6_out, IN[0]);
  and and_1 (and_1_out, d_ff_1_q, not_2_out, IN[3], not_3_out, IN[1], IN[0]);
  and and_2 (and_2_out, d_ff_1_q, not_4_out, IN[3], IN[2], not_5_out, not_6_out);
  or or_1 (CondJump, and_1_out, and_2_out);
  D_Flip_Flop_part d_ff_1 (.clk(CLK), .D(xor_1_out), .Q(d_ff_1_q));  // open: Qn, preset, en, reset
  D_Flip_Flop_part d_ff_2 (.clk(CLK), .D(not_1_out), .Q(d_ff_2_q));  // open: Qn, preset, en, reset
endmodule
